# Fritzing sketch ESP32-CTF-Sketch (saved by Fritzing 0.9.3b)
breadboards: 1

parts:
  U1 = NodeMCU V1.0
  Display1 = LCD screen 16x2 IIC [part_number=101290]
  microSD1 = MicroSD Card Module
  MH-ET_LIVE_ESP32_DEVKIT1 = MH-ET LIVE ESP32 DEVKIT 38 pins

nets:
  N1: U1.RX, MH-ET_LIVE_ESP32_DEVKIT1.TXD0
  N2: U1.TX, MH-ET_LIVE_ESP32_DEVKIT1.RXD0
  GND: Display1.GND, microSD1.GND
  VCC: Display1.VCC, microSD1.VCC
  N3: Display1.SDA, MH-ET_LIVE_ESP32_DEVKIT1.IO21
  N4: Display1.SCL, MH-ET_LIVE_ESP32_DEVKIT1.IO22
  N5: microSD1.MISO, MH-ET_LIVE_ESP32_DEVKIT1.IO19
  N6: microSD1.MOSI, MH-ET_LIVE_ESP32_DEVKIT1.IO23
  N7: microSD1.SCK, MH-ET_LIVE_ESP32_DEVKIT1.IO18
  N8: microSD1.CS, MH-ET_LIVE_ESP32_DEVKIT1.IO5

custom parts:
  NodeMCU V1.0: ESP8266 based NodeMCU
  LCD screen 16x2 IIC: LCD screen with HD44780 controller enables showing text, symbols, value or anything else that comes from Croduino/Arduino. It is capable of showing 16 symbols in two lines and therefore can be used in many projects that need to send clearly visible and legible output information.. • Color of symbols: White • Backlight: Blue • Dimensions: 80 x 36 x 12 mm • Screen dimensions: 64.5 x 16 mm •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
  MH-ET LIVE ESP32 DEVKIT 38 pins: http://mh.nodebb.com/topic/2/mh-et-live-esp32-devkit
