# Fritzing sketch ESP8266-CTF-Sketch (saved by Fritzing 0.9.3b)
circuit board: 8.46667cm x 5.64444cm
breadboards: 1

parts:
  U1 = NodeMCU V1.0
  Display1 = LCD screen 16x2 IIC [part_number=101290]
  microSD1 = MicroSD Card Module
  MH-ET_LIVE_ESP32_DEVKIT1 = MH-ET LIVE ESP32 DEVKIT 38 pins

nets:
  N1: U1.D1, Display1.SCL
  N2: U1.D2, Display1.SDA
  VCC: U1.3V3, Display1.VCC, microSD1.VCC
  GND: U1.GND, Display1.GND, microSD1.GND
  N3: U1.D5, microSD1.SCK
  N4: U1.D6, microSD1.MISO
  N5: U1.D7, microSD1.MOSI
  N6: U1.D8, microSD1.CS
  N7: U1.RX, MH-ET_LIVE_ESP32_DEVKIT1.TXD0
  N8: U1.TX, MH-ET_LIVE_ESP32_DEVKIT1.RXD0

custom parts:
  NodeMCU V1.0: ESP8266 based NodeMCU
  LCD screen 16x2 IIC: LCD screen with HD44780 controller enables showing text, symbols, value or anything else that comes from Croduino/Arduino. It is capable of showing 16 symbols in two lines and therefore can be used in many projects that need to send clearly visible and legible output information.. • Color of symbols: White • Backlight: Blue • Dimensions: 80 x 36 x 12 mm • Screen dimensions: 64.5 x 16 mm •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
  MH-ET LIVE ESP32 DEVKIT 38 pins: http://mh.nodebb.com/topic/2/mh-et-live-esp32-devkit
